# Fritzing sketch Project (saved by Fritzing 0.9.3b)
breadboards: 1

parts:
  U1 = ESP8266 WiFi Module [part_number=ESP8266]
  Componente1 = Arduino Uno (Rev3)
  Part1 = KY-018 Photoresistor Module [package="Breakout board"]

nets:
  N1: U1.RXD, Componente1.D0/RX
  VCC: U1.VCC, U1.CH_PD, Componente1.3V3
  N2: U1.GPIO_0, Componente1.D3_PWM
  GND: U1.GND, Componente1.GND, Part1.-
  N3: U1.TXD, Componente1.D1/TX
  N4: Componente1.A2, Part1.S
  5V: Componente1.5V, Part1.Vin

custom parts:
  ESP8266 WiFi Module: Generic WiFi Module based on the ESP8266 with onboard PCB antenna and UART communications
  KY-018 Photoresistor Module: KY-018 Photoresistor module, used to measure light intensity. It can determine the presence or absence of light.
